// Logisim project seq_circuit.circ as structural Verilog: 1 circuit, main circuit main
module main (
  input  in_1,
  input  in_2,
  output out_3
);

  wire adder_1_cout, clock_1_out, d_ff_1_q;
  wire [7:1] adder_1_out, undriven, undriven_2;

  Adder adder_1 (
    .a({undriven, in_1}), .b({undriven_2, in_2}), .out({adder_1_out, out_3}), .cin(d_ff_1_q),
    .cout(adder_1_cout));
  D_Flip_Flop d_ff_1 (.clk(clock_1_out), .D(adder_1_cout), .Q(d_ff_1_q));  // open: Qn, preset, en, reset
  Clock clock_1 (.out(clock_1_out));
  // Pins of 1 and 8 bits meet at {undriven_2, in_2}
  // Pins of 1 and 8 bits meet at {adder_1_out, out_3}
  // Pins of 1 and 8 bits meet at {undriven, in_1}
endmodule
